# Fritzing sketch MobilitySystem (saved by Fritzing 0.9.3b)

parts:
  M1 = DOIT Esp32 DevKit v1 (30 pins long, 11 pins width) [part_number=ESP32S-PIN30]
  J1 = Basic Servo
  IC1 = L293D [package=THT]
  M2 = Getriebemotor
  BAT1 = Lithium Ion Polymer Battery 11.1v 5000mah
  Buck_Convertor1 = Buck Convertor [part_number=LM2596 package=THT]

nets:
  GND: M1.GND, J1.gnd, IC1.0V, BAT1.negative, Buck_Convertor1.Positive_Input, Buck_Convertor1.Negative_Output
  N1: M1.D25, J1.pulse
  N2: M1.D14, IC1.Enable_1
  N3: M1.D12, IC1.In_2
  N4: M1.D13, IC1.In_1
  VIN: M1.VIN, J1.vcc, IC1.+V, Buck_Convertor1.Positive_Output
  N5: IC1.Out_1_(_Controlled_by_Enable_1_), M2.pin_2
  N6: IC1.Out_2_(_Controlled_by_Enable_1_), M2.pin_1
  N7: IC1.+Vmotor, BAT1.positive, Buck_Convertor1.Negative_Input

custom parts:
  DOIT Esp32 DevKit v1 (30 pins long, 11 pins width): The DOIT Esp32 DevKit v1 is one of the development board created by DOIT to evaluate the ESP-WROOM-32 module. It is based on the ESP32 microcontroller that boasts Wifi, Bluetooth, Ethernet and Low Power support all in a single chip. (vanepp) made breadboard work, adjusted pin numbering and labels and reduced size of schematic and cleaned up pcb. This chip is 30pins long (2 x15) and 11 pins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
  Buck Convertor: DC to DC buck convertor
